// Logisim project d_flipflop_counter.circ as structural Verilog: 2 circuits, main circuit main
module main (
  input  Reset,
  input  [2:0] multiplex
);

  wire clk_out;
  wire [3:0] universal_1_num;

  Clock #(.highDuration(2), .lowDuration(2)) clk (.out(clk_out));
  Clock sysclk ();  // open: out
  Universal universal_1 (.clk(clk_out), .rst(Reset), .out_mux(multiplex), .num(universal_1_num));
  Hex_Digit_Display hex_digit_display_1 (.value(universal_1_num));  // open: dp
  // Probe on universal_1_num

  // Notes on the sheet:
  //   multiplex values:
  //   000 - Up
  //   001 - Down
  //   010 - Decade
endmodule

module Universal (
  input  clk,
  input  rst,
  input  [2:0] out_mux,
  output [3:0] num
);

  wire and_1_out, d_ff_1_qn, d_ff_2_qn, d_ff_3_qn, d_ff_6_qn, d_ff_7_qn, d_ff_8_qn, d_ff_11_qn, d_ff_12_qn,
       d_ff_13_qn, d_ff_16_qn, d_ff_17_qn, d_ff_18_qn, d_ff_20_qn, or_1_out;
  wire [3:0] d_ff_1_q, d_ff_2_q, d_ff_3_q, d_ff_4_q, d_ff_5_q;

  D_Flip_Flop d_ff_1 (.D(d_ff_1_qn), .clk(clk), .Q(d_ff_1_q[0]), .Qn(d_ff_1_qn), .reset(rst));  // open: preset
  D_Flip_Flop d_ff_2 (.D(d_ff_2_qn), .clk(clk), .Q(d_ff_2_q[0]), .Qn(d_ff_2_qn), .preset(rst));  // open: reset
  and and_1 (and_1_out, d_ff_3_q[3], d_ff_3_q[1]);
  D_Flip_Flop d_ff_3 (.D(d_ff_3_qn), .clk(clk), .Q(d_ff_3_q[0]), .Qn(d_ff_3_qn), .reset(or_1_out));  // open: preset
  or or_1 (or_1_out, and_1_out, rst);
  D_Flip_Flop d_ff_4 (.D(d_ff_4_q[3]), .clk(clk), .Q(d_ff_4_q[0]), .preset(rst));  // open: Qn, reset
  D_Flip_Flop d_ff_5 (.D(d_ff_20_qn), .clk(clk), .Q(d_ff_5_q[0]), .preset(rst));  // open: Qn, reset
  D_Flip_Flop d_ff_6 (.D(d_ff_6_qn), .clk(d_ff_1_qn), .Q(d_ff_1_q[1]), .Qn(d_ff_6_qn), .reset(rst));  // open: preset
  D_Flip_Flop d_ff_7 (.D(d_ff_7_qn), .clk(d_ff_2_q[0]), .Q(d_ff_2_q[1]), .Qn(d_ff_7_qn), .preset(rst));  // open: reset
  D_Flip_Flop d_ff_8 (
    .D(d_ff_8_qn), .clk(d_ff_3_qn), .Q(d_ff_3_q[1]), .Qn(d_ff_8_qn), .reset(or_1_out));  // open: preset
  D_Flip_Flop d_ff_9 (.D(d_ff_4_q[0]), .clk(clk), .Q(d_ff_4_q[1]), .reset(rst));  // open: Qn, preset
  D_Flip_Flop d_ff_10 (.D(d_ff_5_q[0]), .clk(clk), .Q(d_ff_5_q[1]), .reset(rst));  // open: Qn, preset
  D_Flip_Flop d_ff_11 (.D(d_ff_11_qn), .clk(d_ff_6_qn), .Q(d_ff_1_q[2]), .Qn(d_ff_11_qn), .reset(rst));  // open: preset
  D_Flip_Flop d_ff_12 (
    .D(d_ff_12_qn), .clk(d_ff_2_q[1]), .Q(d_ff_2_q[2]), .Qn(d_ff_12_qn), .preset(rst));  // open: reset
  D_Flip_Flop d_ff_13 (
    .D(d_ff_13_qn), .clk(d_ff_8_qn), .Q(d_ff_3_q[2]), .Qn(d_ff_13_qn), .reset(or_1_out));  // open: preset
  D_Flip_Flop d_ff_14 (.D(d_ff_4_q[1]), .clk(clk), .Q(d_ff_4_q[2]), .reset(rst));  // open: Qn, preset
  D_Flip_Flop d_ff_15 (.D(d_ff_5_q[1]), .clk(clk), .Q(d_ff_5_q[2]), .reset(rst));  // open: Qn, preset
  D_Flip_Flop d_ff_16 (
    .D(d_ff_16_qn), .clk(d_ff_11_qn), .Q(d_ff_1_q[3]), .Qn(d_ff_16_qn), .reset(rst));  // open: preset
  D_Flip_Flop d_ff_17 (
    .D(d_ff_17_qn), .clk(d_ff_2_q[2]), .Q(d_ff_2_q[3]), .Qn(d_ff_17_qn), .preset(rst));  // open: reset
  D_Flip_Flop d_ff_18 (
    .D(d_ff_18_qn), .clk(d_ff_13_qn), .Q(d_ff_3_q[3]), .Qn(d_ff_18_qn), .reset(or_1_out));  // open: preset
  D_Flip_Flop d_ff_19 (.D(d_ff_4_q[2]), .clk(clk), .Q(d_ff_4_q[3]), .reset(rst));  // open: Qn, preset
  D_Flip_Flop d_ff_20 (.D(d_ff_5_q[2]), .clk(clk), .Q(d_ff_5_q[3]), .Qn(d_ff_20_qn), .reset(rst));  // open: preset
  Multiplexer #(.select(3), .width(4)) multiplexer_1 (
    .in0(d_ff_1_q), .in1(d_ff_2_q), .in2(d_ff_3_q), .in3(d_ff_4_q), .in4(d_ff_5_q), .in5(4'b0000),
    .in6(4'b0000), .in7(4'b0000), .out(num), .sel(out_mux));
endmodule
